// Logisim project C.A(XOR, NAND, NOR)GATES.circ as structural Verilog: 1 circuit, main circuit main
module main (
  input  HALF_ADDER,
  input  in_2,
  input  FULL_ADDER,
  input  in_4,
  input  in_5
);

  wire and_1_out, and_2_out, and_3_out, and_4_out, and_5_out, not_1_out, not_2_out, or_1_out, or_2_out,
       xor_1_out, xor_2_out;

  xor xor_1 (xor_1_out, FULL_ADDER, in_4);
  and and_1 (and_1_out, FULL_ADDER, in_4);
  not not_1 (not_1_out, in_2);
  not not_2 (not_2_out, HALF_ADDER);
  and and_2 (and_2_out, HALF_ADDER, not_1_out);
  xor xor_2 (xor_2_out, xor_1_out, in_5);
  and and_3 (and_3_out, xor_1_out, in_5);
  and and_4 (and_4_out, not_2_out, in_2);
  and and_5 (and_5_out, HALF_ADDER, in_2);
  LED led_1 (.in(xor_2_out));
  or or_1 (or_1_out, and_3_out, and_1_out);
  or or_2 (or_2_out, and_2_out, and_4_out);
  LED led_2 (.in(and_5_out));
  LED led_3 (.in(or_1_out));
  LED led_4 (.in(or_2_out));

  // Notes on the sheet:
  //   CARRY
  //   SUM
endmodule
