// Logisim project lab 8 gates 54765.circ as structural Verilog: 1 circuit, main circuit main
module main (
  input  SR_Flip_Flop,
  input  in_2,
  input  in_3,
  input  in_4,
  input  in_5,
  input  in_6
);

  wire and_1_out, and_2_out, clock_1_out, clock_2_out, clock_3_out, clock_4_out, nand_1_out, nand_2_out,
       nand_3_out, nand_4_out, nand_5_out, nand_6_out, nand_7_out, nand_8_out, nand_9_out, nand_10_out,
       nand_11_out, nand_12_out, nor_1_out, nor_2_out, not_1_out, undriven;

  Clock clock_1 (.out(clock_1_out));
  Clock clock_2 (.out(clock_2_out));
  nand nand_1 (nand_1_out, SR_Flip_Flop, clock_1_out);
  nand nand_2 (nand_2_out, clock_1_out, in_3);
  nand nand_3 (nand_3_out, nand_8_out, in_5, clock_2_out);
  nand nand_4 (nand_4_out, clock_2_out, in_6, nand_7_out);
  nand nand_5 (nand_5_out, nand_1_out, nand_6_out);
  nand nand_6 (nand_6_out, nand_5_out, nand_2_out);
  nand nand_7 (nand_7_out, nand_3_out, nand_8_out);
  nand nand_8 (nand_8_out, nand_7_out, nand_4_out);
  LED led_1 (.in(nand_5_out));
  LED led_2 (.in(nand_6_out));
  LED led_3 (.in(nand_7_out));
  LED led_4 (.in(nand_8_out));
  Clock clock_3 (.out(clock_3_out));
  Clock clock_4 (.out(clock_4_out));
  not not_1 (not_1_out, in_2);
  nand nand_9 (nand_9_out, in_2, undriven);
  nand nand_10 (nand_10_out, undriven, not_1_out, clock_3_out);
  and and_1 (and_1_out, nor_1_out, in_4, clock_4_out);
  and and_2 (and_2_out, clock_4_out, in_4, nor_2_out);
  nand nand_11 (nand_11_out, nand_9_out, nand_12_out);
  nand nand_12 (nand_12_out, nand_11_out, nand_10_out);
  LED led_5 (.in(nand_11_out));
  LED led_6 (.in(nand_12_out));
  nor nor_1 (nor_1_out, and_1_out, nor_2_out);
  nor nor_2 (nor_2_out, nor_1_out, and_2_out);
  LED led_7 (.in(nor_1_out));
  LED led_8 (.in(nor_2_out));

  // Notes on the sheet:
  //   JK Flip Flop
  //   D Flip Flop
  //   T Flip Flop
endmodule
